// Logisim project ALU.circ as structural Verilog
module main (
  input  F0,
  input  [1:0] A,
  input  [1:0] B,
  output Sum_0,
  output Sum_1,
  output Cout_Diff
);

  wire main_1_cout, main_2_cout, not_1_out, xor_1_out, xor_2_out;

  xor xor_1 (xor_1_out, F0, B[0]);
  FullAdder_main main_1 (.A(A[0]), .B(xor_1_out), .Cin(F0), .Sum(Sum_0), .Cout(main_1_cout));
  xor xor_2 (xor_2_out, F0, B[1]);
  FullAdder_main main_2 (.A(A[1]), .B(xor_2_out), .Cin(main_1_cout), .Sum(Sum_1), .Cout(main_2_cout));
  Multiplexer #(.enable("false")) multiplexer_1 (.in0(main_2_cout), .in1(not_1_out), .out(Cout_Diff), .sel(F0));
  not not_1 (not_1_out, main_2_cout);
endmodule

module Inc_Dec (
  input  in_1,
  input  [1:0] in_2,
  output out_3,
  output out_4,
  output out_5
);

  Add_Sub add_sub_1 (.F0(in_1), .A(in_2), .B(2'b01), .Sum_0(out_3), .Sum_1(out_4), .Cout_Diff(out_5));
endmodule

module ALU (
  input  F2,
  input  F1,
  input  F0,
  input  [1:0] A,
  input  [1:0] B,
  output out_6,
  output out_7,
  output out_8,
  output [2:0] out_9
);

  wire Add_Sub_cout_diff, Add_Sub_sum_0, Add_Sub_sum_1, and_1_out, and_2_out, and_3_out, Inc_Decr_out_3,
       Inc_Decr_out_4, Inc_Decr_out_5, nor_1_out, not_1_out;

  nor nor_1 (nor_1_out, F1, F2);
  and and_1 (and_1_out, F0, nor_1_out);
  and and_2 (and_2_out, F0, not_1_out);
  not not_1 (not_1_out, F2);
  and and_3 (and_3_out, and_2_out, F1);
  Add_Sub Add_Sub (
    .F0(and_1_out), .A(A), .B(B), .Sum_0(Add_Sub_sum_0), .Sum_1(Add_Sub_sum_1), .Cout_Diff(Add_Sub_cout_diff));
  Inc_Dec Inc_Decr (.in_1(and_3_out), .in_2(A), .out_3(Inc_Decr_out_3), .out_4(Inc_Decr_out_4), .out_5(Inc_Decr_out_5));
  Multiplexer #(.select(2), .enable("false")) multiplexer_1 (
    .in0(Add_Sub_sum_1), .in1(Add_Sub_sum_1), .in2(Inc_Decr_out_4), .in3(Inc_Decr_out_4), .out(out_7),
    .sel({F1, F0}));
  Multiplexer #(.select(2), .enable("false")) multiplexer_2 (
    .in0(Add_Sub_cout_diff), .in1(Add_Sub_cout_diff), .in2(Inc_Decr_out_5), .in3(Inc_Decr_out_5),
    .out(out_8), .sel({F1, F0}));
  Multiplexer #(.select(2), .enable("false")) multiplexer_3 (
    .in0(Add_Sub_sum_0), .in1(Add_Sub_sum_0), .in2(Inc_Decr_out_3), .in3(Inc_Decr_out_3), .out(out_6),
    .sel({F1, F0}));

  assign out_9 = {out_8, out_7, out_6};
endmodule

module Add_Sub (
  input  F0,
  input  [1:0] A,
  input  [1:0] B,
  output Sum_0,
  output Sum_1,
  output Cout_Diff
);

  wire Full_Adder_2_cout, Full_Adder_cout, not_1_out, xor_1_out, xor_2_out;

  xor xor_1 (xor_1_out, F0, B[0]);
  FullAdder_main Full_Adder (.A(A[0]), .B(xor_1_out), .Cin(F0), .Sum(Sum_0), .Cout(Full_Adder_cout));
  xor xor_2 (xor_2_out, F0, B[1]);
  FullAdder_main Full_Adder_2 (.A(A[1]), .B(xor_2_out), .Cin(Full_Adder_cout), .Sum(Sum_1), .Cout(Full_Adder_2_cout));
  Multiplexer #(.enable("false")) multiplexer_1 (.in0(Full_Adder_2_cout), .in1(not_1_out), .out(Cout_Diff), .sel(F0));
  not not_1 (not_1_out, Full_Adder_2_cout);
endmodule

module A_2 (
  input  [1:0] A,
  input  F0,
  output [1:0] out_3
);

  Multiplexer #(.enable("false")) multiplexer_1 (.in0(A[1]), .in1(1'b0), .out(out_3[1]), .sel(F0));
  Multiplexer #(.enable("false")) multiplexer_2 (.in0(A[0]), .in1(A[1]), .out(out_3[0]), .sel(F0));
endmodule
