// Logisim project ALU.circ as structural Verilog: 11 circuits, main circuit main
module main (
  input  F0,
  input  [1:0] A,
  input  [1:0] B,
  output Sum_0,
  output Sum_1,
  output Cout_Diff
);

  wire main_1_cout, main_2_cout, not_1_out, xor_1_out, xor_2_out;

  xor xor_1 (xor_1_out, F0, B[0]);
  FullAdder_main main_1 (.A(A[0]), .B(xor_1_out), .Cin(F0), .Sum(Sum_0), .Cout(main_1_cout));
  xor xor_2 (xor_2_out, F0, B[1]);
  FullAdder_main main_2 (.A(A[1]), .B(xor_2_out), .Cin(main_1_cout), .Sum(Sum_1), .Cout(main_2_cout));
  Multiplexer #(.enable("false")) multiplexer_1 (.in0(main_2_cout), .in1(not_1_out), .out(Cout_Diff), .sel(F0));
  not not_1 (not_1_out, main_2_cout);
endmodule

module Inc_Dec (
  input  F0,
  input  [1:0] A,
  output Y0,
  output Y1,
  output Carry
);

  Add_Sub add_sub_1 (.F0(F0), .A(A), .B(2'b01), .Sum_0(Y0), .Sum_1(Y1), .Cout_Diff(Carry));
endmodule

module ALU (
  input  F2,
  input  F1,
  input  F0,
  input  [1:0] A,
  input  [1:0] B,
  output out_6,
  output out_7,
  output out_8,
  output [2:0] out_9
);

  wire Add_Sub_cout_diff, Add_Sub_sum_0, Add_Sub_sum_1, and_1_out, and_2_out, and_3_out, Inc_Decr_carry,
       Inc_Decr_y0, Inc_Decr_y1, nor_1_out, not_1_out;

  nor nor_1 (nor_1_out, F1, F2);
  and and_1 (and_1_out, F0, nor_1_out);
  and and_2 (and_2_out, F0, not_1_out);
  not not_1 (not_1_out, F2);
  and and_3 (and_3_out, and_2_out, F1);
  Add_Sub Add_Sub (
    .F0(and_1_out), .A(A), .B(B), .Sum_0(Add_Sub_sum_0), .Sum_1(Add_Sub_sum_1), .Cout_Diff(Add_Sub_cout_diff));
  Inc_Dec Inc_Decr (.F0(and_3_out), .A(A), .Y0(Inc_Decr_y0), .Y1(Inc_Decr_y1), .Carry(Inc_Decr_carry));
  Multiplexer #(.select(2), .enable("false")) multiplexer_1 (
    .in0(Add_Sub_sum_1), .in1(Add_Sub_sum_1), .in2(Inc_Decr_y1), .in3(Inc_Decr_y1), .out(out_7),
    .sel({F1, F0}));
  Multiplexer #(.select(2), .enable("false")) multiplexer_2 (
    .in0(Add_Sub_cout_diff), .in1(Add_Sub_cout_diff), .in2(Inc_Decr_carry), .in3(Inc_Decr_carry),
    .out(out_8), .sel({F1, F0}));
  Multiplexer #(.select(2), .enable("false")) multiplexer_3 (
    .in0(Add_Sub_sum_0), .in1(Add_Sub_sum_0), .in2(Inc_Decr_y0), .in3(Inc_Decr_y0), .out(out_6),
    .sel({F1, F0}));

  assign out_9 = {out_8, out_7, out_6};
endmodule

module Arithmetic (
  input  [1:0] B,
  input  [1:0] A,
  input  F0,
  input  F1,
  output [1:0] Y1Y0,
  output Cout
);

  wire [2:0] add_sub_1_sum_0, inc_dec_1_y0;

  Add_Sub add_sub_1 (
    .F0(F0), .A(A), .B(B), .Sum_0(add_sub_1_sum_0[0]), .Sum_1(add_sub_1_sum_0[1]),
    .Cout_Diff(add_sub_1_sum_0[2]));
  Inc_Dec inc_dec_1 (.F0(F0), .A(A), .Y0(inc_dec_1_y0[0]), .Y1(inc_dec_1_y0[1]), .Carry(inc_dec_1_y0[2]));
  Multiplexer #(.width(3), .enable("false")) multiplexer_1 (
    .in0(add_sub_1_sum_0), .in1(inc_dec_1_y0), .out({Cout, Y1Y0}), .sel(F1));
endmodule

module Add_Sub (
  input  F0,
  input  [1:0] A,
  input  [1:0] B,
  output Sum_0,
  output Sum_1,
  output Cout_Diff
);

  wire Full_Adder_2_cout, Full_Adder_cout, not_1_out, xor_1_out, xor_2_out;

  xor xor_1 (xor_1_out, F0, B[0]);
  FullAdder_main Full_Adder (.A(A[0]), .B(xor_1_out), .Cin(F0), .Sum(Sum_0), .Cout(Full_Adder_cout));
  xor xor_2 (xor_2_out, F0, B[1]);
  FullAdder_main Full_Adder_2 (.A(A[1]), .B(xor_2_out), .Cin(Full_Adder_cout), .Sum(Sum_1), .Cout(Full_Adder_2_cout));
  Multiplexer #(.enable("false")) multiplexer_1 (.in0(Full_Adder_2_cout), .in1(not_1_out), .out(Cout_Diff), .sel(F0));
  not not_1 (not_1_out, Full_Adder_2_cout);
endmodule

module Ax2 (
  input  [1:0] A,
  input  F0,
  output [1:0] Y1Y0,
  output Carry
);

  wire and_2_out, not_1_out;

  and and_1 (Carry, not_1_out, A[1]);
  and and_2 (and_2_out, A[0], not_1_out);
  not not_1 (not_1_out, F0);
  Multiplexer #(.enable("false")) multiplexer_1 (.in0(Carry), .in1(and_2_out), .out(Y1Y0[1]), .sel(not_1_out));
  Multiplexer #(.enable("false")) multiplexer_2 (.in0(and_2_out), .in1(1'b0), .out(Y1Y0[0]), .sel(not_1_out));
endmodule

module A_2 (
  input  [1:0] A,
  input  F0,
  output [1:0] Y1Y0
);

  wire and_1_out, and_2_out;

  and and_1 (and_1_out, F0, A[1]);
  and and_2 (and_2_out, A[0], F0);
  Multiplexer #(.enable("false")) multiplexer_1 (.in0(and_1_out), .in1(1'b0), .out(Y1Y0[1]), .sel(F0));
  Multiplexer #(.enable("false")) multiplexer_2 (.in0(and_2_out), .in1(and_1_out), .out(Y1Y0[0]), .sel(F0));

  // Notes on the sheet:
  //   A1A0
  //   Integer Division
endmodule

module Logic (
  input  [1:0] A,
  input  F0,
  input  F1,
  input  [1:0] B,
  output [1:0] Y1Y0,
  output Carry
);

  wire [1:0] and_1_out, and_2_out, and_3_out, bitwiseandor_1_y1y0, multdiv_1_y0, not_1_out;

  assign and_1_out = A & not_1_out;  // AND_Gate and_1, 2 bits wide
  assign not_1_out = ~{2{F1}};  // NOT_Gate not_1, 2 bits wide
  assign and_2_out = A & {2{F1}};  // AND_Gate and_2, 2 bits wide
  assign and_3_out = B & {2{F1}};  // AND_Gate and_3, 2 bits wide
  MultDiv multdiv_1 (.A(and_1_out), .F0(F0), .Y0(multdiv_1_y0[0]), .Y1(multdiv_1_y0[1]), .Carry(Carry));
  BitwiseANDOR bitwiseandor_1 (.F0(F0), .A(and_2_out), .B(and_3_out), .Y1Y0(bitwiseandor_1_y1y0));
  assign Y1Y0 = multdiv_1_y0 | bitwiseandor_1_y1y0;  // OR_Gate or_1, 2 bits wide

  // Notes on the sheet:
  //   MultDiv
  //   AND OR
  //   Carry Used in Multiply ONLY
endmodule

module MultDiv (
  input  [1:0] A,
  input  F0,
  output Y0,
  output Y1,
  output Carry
);

  wire [1:0] a_2_1_y1y0, ax2_1_y1y0;

  Ax2 ax2_1 (.F0(F0), .Y1Y0(ax2_1_y1y0), .Carry(Carry), .A(A));
  A_2 a_2_1 (.Y1Y0(a_2_1_y1y0), .A(A), .F0(F0));
  or or_1 (Y1, ax2_1_y1y0[1], a_2_1_y1y0[1]);
  or or_2 (Y0, ax2_1_y1y0[0], a_2_1_y1y0[0]);

  // Notes on the sheet:
  //   0:Multiply
  //   1:Divide
  //   Multiply
  //   Divide
endmodule

module BitwiseANDOR (
  input  F0,
  input  [1:0] A,
  input  [1:0] B,
  output [1:0] Y1Y0
);

  wire [1:0] and_1_out, and_2_out, and_3_out, and_4_out, and_5_out, not_1_out, or_1_out;

  assign not_1_out = ~{2{F0}};  // NOT_Gate not_1, 2 bits wide
  assign and_1_out = not_1_out & A;  // AND_Gate and_1, 2 bits wide
  assign and_2_out = B & not_1_out;  // AND_Gate and_2, 2 bits wide
  assign and_3_out = {2{F0}} & A;  // AND_Gate and_3, 2 bits wide
  assign and_4_out = B & {2{F0}};  // AND_Gate and_4, 2 bits wide
  assign and_5_out = and_1_out & and_2_out;  // AND_Gate and_5, 2 bits wide
  assign or_1_out = and_3_out | and_4_out;  // OR_Gate or_1, 2 bits wide
  assign Y1Y0 = and_5_out | or_1_out;  // OR_Gate or_2, 2 bits wide

  // Notes on the sheet:
  //   0:AND
  //   1:OR
  //   Bitwise AND
  //   Bitwise OR
endmodule

module ALUv2 (
  input  [1:0] A,
  input  [1:0] B,
  input  F0,
  input  F1,
  input  F2,
  output [1:0] Y1Y0,
  output Cout
);

  wire [1:0] arithmetic_1_y1y0, logic_1_y1y0;
  wire [2:2] arithmetic_1_cout, logic_1_carry;

  Arithmetic arithmetic_1 (.B(B), .A(A), .F0(F0), .F1(F1), .Y1Y0(arithmetic_1_y1y0), .Cout(arithmetic_1_cout[2]));
  Logic logic_1 (.A(A), .F0(F0), .F1(F1), .B(B), .Y1Y0(logic_1_y1y0), .Carry(logic_1_carry[2]));
  Multiplexer #(.width(3), .enable("false")) multiplexer_1 (
    .in0({arithmetic_1_cout[2], arithmetic_1_y1y0}), .in1({logic_1_carry[2], logic_1_y1y0}),
    .out({Cout, Y1Y0}), .sel(F2));

  // Notes on the sheet:
  //   Arithmetic
  //   Logic
endmodule
