// Logisim project FullAdder.circ as structural Verilog
module main (
  input  A,
  input  B,
  input  Cin,
  output Sum,
  output Cout
);

  wire main_1_out_3, main_1_out_4, main_2_out_4;

  HalfAdder_main main_1 (.A(A), .B(B), .out_3(main_1_out_3), .out_4(main_1_out_4));
  HalfAdder_main main_2 (.A(main_1_out_3), .B(Cin), .out_3(Sum), .out_4(main_2_out_4));
  or or_1 (Cout, main_1_out_4, main_2_out_4);
endmodule
