// Logisim project HalfAdder.circ as structural Verilog: 1 circuit, main circuit main
// HalfAdder
module main (
  input  A,
  input  B,
  output out_3,
  output out_4
);

  xor xor_1 (out_3, A, B);
  and and_1 (out_4, A, B);
endmodule
